// Digital circuit 4bit_ALU.dlogic.dig as structural Verilog
module _4bit_ALU_dlogic (
  input  [3:0] A,
  input  [3:0] B,
  input  Control,
  input  zero,
  output [3:0] Result,
  output Zero_Flag,
  output overflow
);

  // And and_1 has open pins: In_1=A, In_2=B, out=open
  // Or or_1 has open pins: In_1=A, In_2=B, out=open
  // XOr xor_1 has open pins: In_1=A, In_2=B, out=open
  // _4bit_full_adder _4bit_full_adder_1: pin names not known; wires that end beside it: zero, A, B, Result, overflow

  assign Zero_Flag = zero;
endmodule
